# Fritzing sketch TasmotaGasMeter (saved by Fritzing 0.9.3b)

parts:
  WeMos_D1_Mini1 = WeMos D1 Mini
  C1 = Electrolytic Capacitor [capacitance=1µF package="100 mil [THT, electrolytic]"]
  C2 = Ceramic Capacitor [capacitance=100nF package="100 mil [THT, multilayer]"]
  S1 = Reed switch [part_number=IN-Z61 package=THT]
  LED1 = LED - 5mm [color="Green (570nm)" package="5 mm [THT]"]
  R1 = Resistor [tolerance=±5% resistance=220 package=THT]
  R2 = Resistor [tolerance=±5% resistance=220 package=THT]
  LED2 = LED - 5mm [color="Red (633nm)" package="5 mm [THT]"]

nets:
  N1: WeMos_D1_Mini1.3V3, C1.+, C2.0
  5V: WeMos_D1_Mini1.5V
  N2: WeMos_D1_Mini1.D1, R2.Pin_1
  N3: WeMos_D1_Mini1.D2, R1.Pin_1
  N4: WeMos_D1_Mini1.D4, S1.pin_1
  GND: WeMos_D1_Mini1.G, C1.-, C2.1, S1.pin_2, LED1.cathode, LED2.cathode
  N5: LED1.anode, R1.Pin_0
  N6: R2.Pin_0, LED2.anode

notes:
  5V
